# Fritzing sketch radio_pcb (saved by Fritzing 0.9.10b)
circuit board: 6.49297cm x 2.99217cm
breadboards: 1

parts:
  MCU1 = Raspberry Pi Zero
  R1 = Resistor [tolerance=±10% resistance=1000 power=0.25 package=THT]
  R2 = Resistor [tolerance=±10% resistance=1000 power=0.25 package=THT]
  R3 = Resistor [tolerance=±10% resistance=1000 power=0.25 package=THT]
  R4 = Resistor [tolerance=±10% resistance=1000 power=0.25 package=THT]
  R5 = Resistor [tolerance=±10% resistance=1000 power=0.25 package=THT]
  R6 = Resistor [tolerance=±10% resistance=1000 power=0.25 package=THT]
  volume_control = male pin header, 5 pins [form="♂ (male)"]
  selector = male pin header, 5 pins [form="♂ (male)"]
  LED = male pin header, 4 pins [form="♂ (male)"]
  Logic_converter = Logic Level Converter

nets:
  N1: MCU1.pin_1, MCU1.pin_17, volume_control.pin2, volume_control.pin4, selector.pin2, selector.pin4, Logic_converter.TX2_HV
  N2: MCU1.pin_2, MCU1.pin_4, LED.pin3, Logic_converter.TX2_LV
  N3: MCU1.pin_3, LED.pin2, Logic_converter.GND
  N4: MCU1.pin_5, Logic_converter.RX2_HV
  N5: MCU1.pin_6, MCU1.pin_9, MCU1.pin_14, MCU1.pin_20, MCU1.pin_25, LED.pin4, Logic_converter.TX_LV, Logic_converter.TX_HV
  N6: MCU1.pin_11, R4.Pin_0
  N7: MCU1.pin_13, R5.Pin_0
  N8: MCU1.pin_15, R6.Pin_0
  N9: MCU1.pin_29, R1.Pin_0
  N10: MCU1.pin_31, R2.Pin_0
  N11: MCU1.pin_33, R3.Pin_0
  N12: R1.Pin_1, selector.pin5
  N13: R2.Pin_1, selector.pin3
  N14: R3.Pin_1, selector.pin1
  N15: R4.Pin_1, volume_control.pin1
  N16: R5.Pin_1, volume_control.pin3
  N17: R6.Pin_1, volume_control.pin5
  N18: LED.pin1, Logic_converter.RX2_LV
